# Fritzing sketch SmartGarden (saved by Fritzing 0.9.4)
breadboards: 2

parts:
  U1 = LuaNode32 / ESP32
  S1 = H-Bridge with L298N
  R1 = Resistor [tolerance=±5% resistance=10k package="1206 [SMD]"]
  Componente1 = Soil Moisture Sensor
  M1 = DC Motor
  Componente2 = GUVA-S12SD UV Light Sensor
  KY-1 = Keyes Relay [package=THT]
  Power_plug1 = Power plug
  DHT2 = DHT22 Humidity and Temperature Sensor
  Squix2 = OLED 0.96" 128x64 I2C SSD1306 (GND/VCC)
  LED2 = LEDs [package=led10mm]
  R2 = Resistor [tolerance=±5% resistance=10k package="1206 [SMD]"]

nets:
  N1: U1.D34, Componente2.Out
  N2: U1.D32, KY-1.signal
  N3: U1.D33, Componente1.SIG
  N4: U1.D27, R1.Pin_1, DHT2.DATA
  GND: U1.GND, Componente1.GND, Componente2.GND, KY-1.ground, DHT2.GND, Squix2.GND
  VIN: U1.Vin, Componente2.5V, KY-1.power, Squix2.VCC
  3V3: U1.3V3, R1.Pin_0, DHT2.VDD, R2.Pin_1
  N5: U1.D2, S1.ENA
  N6: U1.D4, R2.Pin_0
  N7: U1.D18, S1.IN1
  N8: U1.D19, S1.IN2
  N9: U1.D21, Componente1.VCC
  N10: U1.D22, Squix2.SCA
  N11: U1.D23, Squix2.SCL
  GND_2: S1.GND, Power_plug1.GND
  5V: S1.5V, Power_plug1.VCC
  N12: S1.M1-01, M1.pin_1
  N13: S1.M1-02, M1.pin_2
  N14: KY-1.NC, LED2.A

custom parts:
  LuaNode32 / ESP32: ESP32 based LuaNode32
  H-Bridge with L298N: h-bridge
  GUVA-S12SD UV Light Sensor: Extend your light-sensing spectrum with this analog UV sensor module. It uses a UV photodiode, which can detect the 240-370nm range of light (which covers UVB and most of UVA spectrum). The signal level from the photodiode is very small, in the nano-ampere level, so we tossed on an opamp to amplify the signal to a more manageable volt-level.
  Keyes Relay: The Keyes 5V relay module is suitable for SCM development, home appliance control. It uses a 5V~12V TIL control signal which can control DC / AC signal.
  OLED 0.96" 128x64 I2C SSD1306 (GND/VCC): OLED 0.96" 128x64 I2C SSD1306 Pinout: GND/VCC/SCL/SDA
  LEDs: LEDs Standard schematic elements and footprints for 5mm, 3mm, 1206, and 0603 sized LEDs. 5mm - Spark Fun Electronics SKU : COM-00529 (and others)
